# Fritzing sketch analog_inputA (saved by Fritzing 0.7.10b)
breadboards: 2

parts:
  R1 = Resistor [tolerance=±5% resistance=10k package=THT]
  C1 = Ceramic Capacitor [capacitance=100nF package="100 mil [THT, multilayer]"]
  R2 = Rotary Potentiometer (Small) [maximum_resistance=100kΩ]
  LED1 = LED - 5mm [color="Red (633nm)" package="5 mm [THT]"]
  LED2 = LED - 5mm [color="Red (633nm)" package="5 mm [THT]"]
  LED3 = LED - 5mm [color="Red (633nm)" package="5 mm [THT]"]
  LED4 = LED - 5mm [color="Red (633nm)" package="5 mm [THT]"]
  LED5 = LED - 5mm [color="Red (633nm)" package="5 mm [THT]"]
  LED6 = LED - 5mm [color="Red (633nm)" package="5 mm [THT]"]
  LED7 = LED - 5mm [color="Red (633nm)" package="5 mm [THT]"]
  LED8 = LED - 5mm [color="Red (633nm)" package="5 mm [THT]"]
  U1 = mystery part, 20 pins [chip_label=?]
  VCC1 = Battery

nets:
  N1: R1.Pin_0, C1.1, U1.pin4
  N2: C1.0, R2.leg2, LED1.cathode, LED2.cathode, LED3.cathode, LED4.cathode, LED5.cathode, LED6.cathode, LED7.cathode, LED8.cathode, U1.pin1, U1.pin2, U1.pin7, U1.pin8, U1.pin10, VCC1.-
  N3: R2.leg1, VCC1.+
  N4: R2.wiper, U1.pin6
  N5: LED1.anode, U1.pin12
  N6: LED2.anode, U1.pin11
  N7: LED3.anode, U1.pin13
  N8: LED4.anode, U1.pin14
  N9: LED5.anode, U1.pin15
  N10: LED6.anode, U1.pin16
  N11: LED7.anode, U1.pin17
  N12: LED8.anode, U1.pin18
  N13: U1.pin3, U1.pin5
