# Fritzing sketch buttons (saved by Fritzing 0.7.10b)
breadboards: 1

parts:
  Raspberry_Pi1 = Raspberry Pi (Model B)
  S1 = Pushbutton [package="[THT]"]
  S2 = Pushbutton [package="[THT]"]
  S3 = Pushbutton [package="[THT]"]
  S4 = Pushbutton [package="[THT]"]
  S5 = Pushbutton [package="[THT]"]
  S6 = Pushbutton [package="[THT]"]
  R1 = Resistor [tolerance=±5% resistance=220 package=THT]
  R2 = Resistor [tolerance=±5% resistance=220 package=THT]
  R3 = Resistor [tolerance=±5% resistance=220 package=THT]
  R4 = Resistor [tolerance=±5% resistance=220 package=THT]
  R5 = Resistor [tolerance=±5% resistance=220 package=THT]
  R6 = Resistor [tolerance=±5% resistance=220 package=THT]

nets:
  N1: Raspberry_Pi1.5V, R1.Pin_0, R2.Pin_0, R3.Pin_0, R4.Pin_0, R5.Pin_0, R6.Pin_0
  N2: Raspberry_Pi1.GND, S1.Pin_3, S1.Pin_4, S2.Pin_3, S2.Pin_4, S3.Pin_3, S3.Pin_4, S5.Pin_3, S5.Pin_4, S6.Pin_3, S6.Pin_4
  N3: Raspberry_Pi1.#17, S1.Pin_1, S1.Pin_2, R1.Pin_1
  N4: Raspberry_Pi1.#23, S5.Pin_1, S5.Pin_2, R6.Pin_1
  N5: Raspberry_Pi1.MOSI, S2.Pin_1, S2.Pin_2, R2.Pin_1
  N6: Raspberry_Pi1.MISO, S4.Pin_1, S4.Pin_2, R4.Pin_1
  N7: Raspberry_Pi1.#25, S3.Pin_1, S3.Pin_2, R3.Pin_1
  N8: Raspberry_Pi1.CS1, S6.Pin_1, S6.Pin_2, R5.Pin_1
  N9: S4.Pin_3, S4.Pin_4

custom parts:
  Raspberry Pi (Model B): Raspberry Pi Single-board Computer, Model B
