# Fritzing sketch irread (saved by Fritzing 0.7.10b)
breadboards: 1

parts:
  U1 = mystery part, 3 pins [chip_label=?]
  U1_2 = mystery part, 3 pins [chip_label=?]
  Raspberry_Pi1 = Raspberry Pi (Model B)

nets:
  N1: U1.pin1, U1_2.pin1, Raspberry_Pi1.5V
  N2: U1.pin2, U1_2.pin2, Raspberry_Pi1.GND
  N3: U1.pin3, U1_2.pin3, Raspberry_Pi1.CS0

custom parts:
  Raspberry Pi (Model B): Raspberry Pi Single-board Computer, Model B
