# Fritzing sketch ir2led (saved by Fritzing 0.7.10b)
breadboards: 1

parts:
  U1 = mystery part, 3 pins [chip_label=?]
  U1_2 = mystery part, 3 pins [chip_label=?]
  Raspberry_Pi1 = Raspberry Pi (Model B)
  LED1 = LED - 5mm [color="Red (633nm)" package="5 mm [THT]"]
  LED2 = LED - 5mm [color="Red (633nm)" package="5 mm [THT]"]

nets:
  N1: U1.pin1, U1_2.pin1, Raspberry_Pi1.5V
  N2: U1.pin2, U1_2.pin2, Raspberry_Pi1.GND, LED1.cathode, LED2.cathode
  N3: U1.pin3, U1_2.pin3, Raspberry_Pi1.CS0
  N4: Raspberry_Pi1.MISO, LED1.anode
  N5: Raspberry_Pi1.#25, LED2.anode

custom parts:
  Raspberry Pi (Model B): Raspberry Pi Single-board Computer, Model B
