# Fritzing sketch NPNSpeed (saved by Fritzing 0.7.10b)
breadboards: 1

parts:
  M1 = DC Motor
  Q1 = NPN-Transistor [package="TO92 [THT]"]
  Raspberry_Pi1 = Raspberry Pi (Model B)
  R1 = Resistor [tolerance=±5% resistance=220 package=THT]
  D1 = Rectifier Diode [part_number=1N4001 package="300 mil [THT]"]

nets:
  N1: M1.pin_1, Raspberry_Pi1.5V, D1.cathode
  N2: M1.pin_2, Q1.C, D1.anode
  N3: Q1.E, Raspberry_Pi1.GND
  N4: Q1.B, R1.Pin_1
  N5: Raspberry_Pi1.#4, R1.Pin_0

custom parts:
  Raspberry Pi (Model B): Raspberry Pi Single-board Computer, Model B
