# Fritzing sketch L293D_2 (saved by Fritzing 0.7.10b)
breadboards: 1

parts:
  M1 = DC Motor
  Raspberry_Pi1 = Raspberry Pi (Model B)
  IC1 = L293D [package=THT]
  VCC1 = Battery block 9V

nets:
  N1: M1.pin_1, IC1.Out_2_(_Controlled_by_Enable_1_)
  N2: M1.pin_2, IC1.Out_1_(_Controlled_by_Enable_1_)
  N3: Raspberry_Pi1.5V, IC1.+V
  N4: Raspberry_Pi1.GND, IC1.0V, VCC1.-
  N5: Raspberry_Pi1.#17, IC1.In_1
  N6: Raspberry_Pi1.#18, IC1.In_2
  N7: Raspberry_Pi1.#21, IC1.Enable_1
  N8: IC1.+Vmotor, VCC1.+

custom parts:
  Raspberry Pi (Model B): Raspberry Pi Single-board Computer, Model B
