# Fritzing sketch pwm (saved by Fritzing 0.9.0b)
breadboards: 1

parts:
  R2 = Resistor [tolerance=±5% resistance=10k package=THT]
  LED2 = LED - 5mm [color="Red (633nm)" package="5 mm [THT]"]
  Raspberry_Pi1 = Raspberry Pi (Model B)

nets:
  N1: R2.Pin_0, Raspberry_Pi1.GND
  N2: R2.Pin_1, LED2.cathode

custom parts:
  Raspberry Pi (Model B): Raspberry Pi Single-board Computer, Model B
