# Fritzing sketch pwm_Robots (saved by Fritzing 0.7.10b)
breadboards: 1

parts:
  Raspberry_Pi1 = Raspberry Pi (Model B)
  Power_plug1 = Power plug
  J1 = Basic Servo
  J2 = Basic Servo

nets:
  GND: Raspberry_Pi1.GND, Power_plug1.GND, J2.gnd
  N1: Raspberry_Pi1.#17, J1.pulse
  N2: Raspberry_Pi1.#18, J2.pulse
  VCC: Power_plug1.VCC, J1.vcc, J2.vcc

custom parts:
  Raspberry Pi (Model B): Raspberry Pi Single-board Computer, Model B
