# Fritzing sketch pwm_Servo (saved by Fritzing 0.7.10b)
breadboards: 1

parts:
  Raspberry_Pi1 = Raspberry Pi (Model B)
  Power_plug1 = Power plug
  J1 = Basic Servo

nets:
  GND: Raspberry_Pi1.GND, Power_plug1.GND, J1.gnd

custom parts:
  Raspberry Pi (Model B): Raspberry Pi Single-board Computer, Model B
